// Logisim project cpu.circ as structural Verilog: 1 circuit, main circuit cpu
module cpu (
  input  clk,
  input  [31:0] INSTRUCTION,
  input  [31:0] READ_DATA,
  output [31:0] WRITE_ADDRESS,
  output [31:0] PROGRAM_COUNTER,
  output [31:0] ra,
  output [31:0] sp,
  output [31:0] t0,
  output [31:0] t1,
  output [31:0] t2,
  output [31:0] s0,
  output [31:0] s1,
  output [31:0] a0,
  output [31:0] tohost,
  output [3:0] WRITE_ENABLE,
  output [31:0] WRITE_DATA
);

  wire ASel, BrEq, BrLt, BrUn, BSel, control_logic_1_pcsel, MemRW, RegWEn;
  wire [1:0] WBSel;
  wire [2:0] ImmSel;
  wire [3:0] ALUSel;
  wire [31:0] Imm, multiplexer_1_out, multiplexer_2_out, multiplexer_3_out, PC_PLUS_4, Reg_Write_Data,
       regfile_1_read_data_1, regfile_1_read_data_2;

  Multiplexer #(.enable("false"), .width(32)) multiplexer_1 (
    .in0(PC_PLUS_4), .in1(WRITE_ADDRESS), .out(multiplexer_1_out), .sel(control_logic_1_pcsel));
  control_logic control_logic_1 (
    .PCSel(control_logic_1_pcsel), .RegWEn(RegWEn), .ImmSel(ImmSel), .BrUn(BrUn), .ASel(ASel), .BSel(BSel),
    .ALUSel(ALUSel), .MemRW(MemRW), .WBSel(WBSel), .inst(INSTRUCTION), .BrEq(BrEq), .BrLt(BrLt));  // open: CSRWen, CSRSel
  Register #(.width(32)) PC (.D(multiplexer_1_out), .clk(clk), .Q(PROGRAM_COUNTER));  // open: en, clr
  Adder #(.width(32)) adder_1 (.a(32'h4), .b(PROGRAM_COUNTER), .out(PC_PLUS_4));  // open: cin, cout
  imm_gen imm_gen_1 (.inst(INSTRUCTION), .ImmSel(ImmSel), .imm(Imm));
  regfile regfile_1 (
    .rs1(INSTRUCTION[19:15]), .rs2(INSTRUCTION[24:20]), .rd(INSTRUCTION[11:7]), .Write_Data(Reg_Write_Data),
    .RegWEn(RegWEn), .clk(clk), .ra(ra), .sp(sp), .t0(t0), .t1(t1), .t2(t2), .s0(s0), .s1(s1), .a0(a0),
    .Read_Data_1(regfile_1_read_data_1), .Read_Data_2(regfile_1_read_data_2));
  branch_comp branch_comp_1 (
    .rs1(regfile_1_read_data_1), .rs2(regfile_1_read_data_2), .BrUn(BrUn), .BrEq(BrEq), .BrLt(BrLt));
  Multiplexer #(.enable("false"), .width(32)) multiplexer_2 (
    .in0(regfile_1_read_data_1), .in1(PROGRAM_COUNTER), .out(multiplexer_2_out), .sel(ASel));
  Multiplexer #(.enable("false"), .width(32)) multiplexer_3 (
    .in0(regfile_1_read_data_2), .in1(Imm), .out(multiplexer_3_out), .sel(BSel));
  alu alu_1 (.Result(WRITE_ADDRESS), .A(multiplexer_2_out), .B(multiplexer_3_out), .ALUSel(ALUSel));
  Multiplexer #(.enable("false"), .select(2), .width(32)) multiplexer_4 (
    .in0(READ_DATA), .in1(WRITE_ADDRESS), .in2(PC_PLUS_4), .out(Reg_Write_Data), .sel(WBSel));  // open: in3
  csr csr_1 (.tohost(tohost));  // open: CSR_address, CSR_din, CSR_WE, clk

  // Other names for the same wires on the sheet: ALU_RES[31:0] = WRITE_ADDRESS; rd[4:0] = INSTRUCTION[11:7];
  //   rs1[4:0] = INSTRUCTION[19:15]; rs2[4:0] = INSTRUCTION[24:20]

  // Notes on the sheet:
  //   Output to IMEM
  //   IMEM (do **NOT** move this)
  //   Inputs from IMEM
  //   It is OK to move the PC, RegFile, ALU, MEM, Branch Comp, Imm Gen, and Control Logic to wherever is most convenient for you when constructing your CPU, and to delete this text
  //   Inputs/Outputs for testing. Do **NOT** move these.
  //   Outputs To DMEM
  //   DMEM (do **NOT** move this)
  //   Inputs From DMEM
endmodule
